// Digital circuit 3_bit_AND_gate_w_splitter.dig as structural Verilog
module _3_bit_AND_gate_w_splitter (
  input  [2:0] A_3,
  input  [2:0] B_3,
  output Out
);

  wire and_1_out, and_2_out, and_3_out, and_4_out;

  and and_1 (and_1_out, A_3[0], B_3[0]);
  and and_2 (and_2_out, A_3[1], B_3[1]);
  and and_3 (and_3_out, A_3[2], B_3[2]);
  and and_4 (and_4_out, and_1_out, and_2_out);
  and and_5 (Out, and_4_out, and_3_out);
endmodule
