// Digital circuit 4_bit_adder.dig as structural Verilog
module _4_bit_adder (
  input  A_0,
  input  B_0,
  input  A_1,
  input  B_1,
  input  A_2,
  input  B_2,
  input  A_3,
  input  B_3,
  input  Carry_in,
  output Out_0,
  output Carry_out,
  output Out_1,
  output Out_2,
  output Out_3
);

  wire full_adder_1_out_b, full_adder_2_out_b, full_adder_3_out_b;

  full_adder full_adder_4 (.Carryin(full_adder_3_out_b), .A_in(A_3), .B_in(B_3), .Out_A(Out_3), .Out_B(Carry_out));
  full_adder full_adder_3 (
    .Carryin(full_adder_2_out_b), .A_in(A_2), .B_in(B_2), .Out_A(Out_2), .Out_B(full_adder_3_out_b));
  full_adder full_adder_2 (
    .Carryin(full_adder_1_out_b), .A_in(A_1), .B_in(B_1), .Out_A(Out_1), .Out_B(full_adder_2_out_b));
  full_adder full_adder_1 (.Carryin(Carry_in), .A_in(A_0), .B_in(B_0), .Out_A(Out_0), .Out_B(full_adder_1_out_b));
endmodule
