// Digital circuit 8-bit-latch.dig as structural Verilog
module _8_bit_latch (
  input  D0,
  input  D1,
  input  D2,
  input  D3,
  input  D4,
  input  D5,
  input  D6,
  input  D7,
  input  Clk,
  output Q3,
  output Q1,
  output Q4,
  output Q5,
  output Q6,
  output Q7,
  output Q2,
  output Q0,
  output Q_0,
  output Q_1,
  output Q_2,
  output Q_3,
  output Q_4,
  output Q_5,
  output Q_6,
  output Q_7
);

  level_trig_D_type_Flip_Flop level_trig_d_type_flip_flop_1 (.Hold_That_Bit(Clk), .Data(D7), .Q(Q7), .Q_2(Q_7));
  level_trig_D_type_Flip_Flop level_trig_d_type_flip_flop_2 (.Hold_That_Bit(Clk), .Data(D6), .Q(Q6), .Q_2(Q_6));
  level_trig_D_type_Flip_Flop level_trig_d_type_flip_flop_3 (.Hold_That_Bit(Clk), .Data(D5), .Q(Q5), .Q_2(Q_5));
  level_trig_D_type_Flip_Flop level_trig_d_type_flip_flop_4 (.Hold_That_Bit(Clk), .Data(D4), .Q(Q4), .Q_2(Q_4));
  level_trig_D_type_Flip_Flop level_trig_d_type_flip_flop_5 (.Hold_That_Bit(Clk), .Data(D3), .Q(Q3), .Q_2(Q_3));
  level_trig_D_type_Flip_Flop level_trig_d_type_flip_flop_6 (.Hold_That_Bit(Clk), .Data(D2), .Q(Q2), .Q_2(Q_2));
  level_trig_D_type_Flip_Flop level_trig_d_type_flip_flop_7 (.Hold_That_Bit(Clk), .Data(D1), .Q(Q1), .Q_2(Q_1));
  level_trig_D_type_Flip_Flop level_trig_d_type_flip_flop_8 (.Hold_That_Bit(Clk), .Data(D0), .Q(Q0), .Q_2(Q_0));
endmodule
