// Digital circuit AND from NAND.dig as structural Verilog
module AND_from_NAND (
  input  in_1,
  input  in_2,
  output out_3
);

  wire nand_1_out, nand_2_out;

  nand nand_1 (nand_1_out, in_1, in_2);
  nand nand_2 (nand_2_out, in_1, in_2);
  nand nand_3 (out_3, nand_1_out, nand_2_out);
endmodule
