// Digital circuit Adding Machine-2.dig as structural Verilog
module Adding_Machine_2 (
  input  in_6,
  output out_1,
  output out_2,
  output out_3,
  output out_4,
  output out_5,
  output out_7,
  output out_8
);

  wire _2_to_1_sel_1_out, _8_bit_latch_1_q3;

  _2_to_1_sel _2_to_1_sel_1 (.A(out_4), .B(_8_bit_latch_1_q3), .Sel(out_7), .Out(_2_to_1_sel_1_out));
  Eight_Bit_Adder eight_bit_adder_1 (
    .ci(out_8), .a0(out_3), .b0(_2_to_1_sel_1_out), .a1(out_3), .b1(_2_to_1_sel_1_out), .a2(out_3),
    .a3(out_3), .a4(out_3), .a5(out_3), .a6(out_3), .a7(out_3), .b2(_2_to_1_sel_1_out),
    .b3(_2_to_1_sel_1_out), .b4(_2_to_1_sel_1_out), .b5(_2_to_1_sel_1_out), .b6(_2_to_1_sel_1_out),
    .b7(_2_to_1_sel_1_out), .o0(out_1), .o1(out_1), .o2(out_1), .o3(out_1), .o4(out_1), .o5(out_1),
    .o6(out_1), .o7(out_1), .co(out_2));
  _8_bit_latch _8_bit_latch_1 (
    .D0(out_1), .D1(out_1), .D2(out_1), .D3(out_1), .D4(out_1), .D5(out_1), .D6(out_1), .D7(out_1),
    .Clk(out_5), .Q3(_8_bit_latch_1_q3), .Q1(_8_bit_latch_1_q3), .Q4(_8_bit_latch_1_q3),
    .Q5(_8_bit_latch_1_q3), .Q6(_8_bit_latch_1_q3), .Q7(_8_bit_latch_1_q3), .Q2(_8_bit_latch_1_q3),
    .Q0(_8_bit_latch_1_q3), .Q_0(in_6), .Q_1(in_6), .Q_2(in_6), .Q_3(in_6), .Q_4(in_6), .Q_5(in_6),
    .Q_6(in_6), .Q_7(in_6));
endmodule
