// Digital circuit Hold-that-bit-with-r-s-flip-flop.dig as structural Verilog
module Hold_that_bit_with_r_s_flip_flop (
  input  Reset,
  input  Hold_That_Bit,
  input  Set,
  output Q,
  output Q_2
);

  wire and_1_out, and_2_out;

  and and_1 (and_1_out, Reset, Hold_That_Bit);
  and and_2 (and_2_out, Hold_That_Bit, Set);
  R_S_flip_flop r_s_flip_flop_1 (.R(and_1_out), .S(and_2_out), .Q(Q), .Q_2(Q_2));
endmodule
