// Digital circuit Subtraction.dig as structural Verilog
module Subtraction (
  input  b0,
  input  b1,
  input  b2,
  input  b3,
  input  b4,
  input  b5,
  input  b6,
  input  b7,
  input  Invert,
  input  a1,
  input  a2,
  input  a3,
  input  a4,
  input  a5,
  input  a0,
  input  a6,
  input  a7,
  input  SUB,
  input  SUB_2,
  output o1,
  output o0,
  output o2,
  output o3,
  output o4,
  output o5,
  output o6,
  output o7,
  output Overflow
);

  wire eight_bit_adder_1_co, ones_comp_1_o0, ones_comp_1_o1, ones_comp_1_o2, ones_comp_1_o3, ones_comp_1_o4,
       ones_comp_1_o5, ones_comp_1_o6, ones_comp_1_o7;

  or or_1 (Overflow, SUB, eight_bit_adder_1_co);
  Eight_Bit_Adder eight_bit_adder_1 (
    .ci(SUB_2), .a0(a0), .b0(ones_comp_1_o0), .a1(a1), .b1(ones_comp_1_o1), .a2(a2), .a3(a3), .a4(a4),
    .a5(a5), .a6(a6), .a7(a7), .b2(ones_comp_1_o2), .b3(ones_comp_1_o3), .b4(ones_comp_1_o4),
    .b5(ones_comp_1_o5), .b6(ones_comp_1_o6), .b7(ones_comp_1_o7), .o0(o0), .o1(o1), .o2(o2), .o3(o3),
    .o4(o4), .o5(o5), .o6(o6), .o7(o7), .co(eight_bit_adder_1_co));
  Ones_Comp ones_comp_1 (
    .Invert(Invert), .i7(b7), .i6(b6), .i5(b5), .i4(b4), .i3(b3), .i2(b2), .i1(b1), .i0(b0),
    .o7(ones_comp_1_o7), .o6(ones_comp_1_o6), .o5(ones_comp_1_o5), .o4(ones_comp_1_o4), .o3(ones_comp_1_o3),
    .o2(ones_comp_1_o2), .o1(ones_comp_1_o1), .o0(ones_comp_1_o0));
endmodule
