// Digital circuit level-trig-D-type-Flip-Flop.dig as structural Verilog
module level_trig_D_type_Flip_Flop (
  input  Hold_That_Bit,
  input  Data,
  output Q,
  output Q_2
);

  wire and_1_out, and_2_out, not_1_out;

  not not_1 (not_1_out, Data);
  and and_1 (and_1_out, not_1_out, Hold_That_Bit);
  and and_2 (and_2_out, Hold_That_Bit, Data);
  R_S_flip_flop r_s_flip_flop_1 (.R(and_1_out), .S(and_2_out), .Q(Q), .Q_2(Q_2));
endmodule
