// Digital circuit mux4way.dig as structural Verilog
module mux4way (
  input  In,
  input  Sel1,
  input  Sel2,
  output A,
  output B,
  output C,
  output D
);

  wire not_1_out, not_2_out;

  not not_1 (not_1_out, Sel1);
  not not_2 (not_2_out, Sel2);
  and and_1 (A, In, not_1_out, not_2_out);
  and and_2 (B, In, not_1_out, Sel2);
  and and_3 (C, In, Sel1, not_2_out);
  and and_4 (D, In, Sel1, Sel2);
endmodule
