// Digital circuit xor.dig as structural Verilog
module \xor  (
  input  InA,
  input  InB,
  output Out
);

  wire and_1_out, not_1_out, or_1_out;

  or or_1 (or_1_out, InA, InB);
  and and_1 (and_1_out, InA, InB);
  not not_1 (not_1_out, and_1_out);
  and and_2 (Out, or_1_out, not_1_out);
endmodule
