// Digital circuit xorOnMyOwn.dig as structural Verilog
module xorOnMyOwn (
  input  Ain,
  input  Bin,
  output out
);

  wire nand_1_out, or_1_out;

  or or_1 (or_1_out, Bin, Ain);
  nand nand_1 (nand_1_out, Ain, Bin);
  and and_1 (out, or_1_out, nand_1_out);
endmodule
