// Digital circuit 6_bit_AND.dig as structural Verilog
module _6_bit_AND (
  input  [5:0] A_6,
  input  [5:0] B_6,
  output Out
);

  wire _3_bit_and_gate_w_splitter_1_out, _3_bit_and_gate_w_splitter_2_out;

  _3_bit_AND_gate_w_splitter _3_bit_and_gate_w_splitter_1 (
    .A_3(A_6[2:0]), .B_3(B_6[2:0]), .Out(_3_bit_and_gate_w_splitter_1_out));
  _3_bit_AND_gate_w_splitter _3_bit_and_gate_w_splitter_2 (
    .A_3(A_6[5:3]), .B_3(B_6[5:3]), .Out(_3_bit_and_gate_w_splitter_2_out));
  and and_1 (Out, _3_bit_and_gate_w_splitter_1_out, _3_bit_and_gate_w_splitter_2_out);
endmodule
