// Digital circuit Adding Machine.dig as structural Verilog
module Adding_Machine (
  input  D0,
  input  D1,
  input  D2,
  input  D3,
  input  D4,
  input  D5,
  input  D6,
  input  D7,
  input  Clk,
  output Q3,
  output Q1,
  output Q4,
  output Q5,
  output Q6,
  output Q7,
  output Q2,
  output Q0
);

  level_trig_D_type_Flip_Flop level_trig_d_type_flip_flop_1 (.Hold_That_Bit(Clk), .Data(D7), .Q(Q7));  // open: Q_2
  level_trig_D_type_Flip_Flop level_trig_d_type_flip_flop_2 (.Hold_That_Bit(Clk), .Q(Q6));  // open: Data, Q_2
  level_trig_D_type_Flip_Flop level_trig_d_type_flip_flop_3 (.Hold_That_Bit(Clk), .Data(D6), .Q(Q5));  // open: Q_2
  level_trig_D_type_Flip_Flop level_trig_d_type_flip_flop_4 (.Hold_That_Bit(Clk), .Data(D5), .Q(Q4));  // open: Q_2
  level_trig_D_type_Flip_Flop level_trig_d_type_flip_flop_5 (.Hold_That_Bit(Clk), .Data(D4), .Q(Q3));  // open: Q_2
  level_trig_D_type_Flip_Flop level_trig_d_type_flip_flop_6 (.Hold_That_Bit(Clk), .Data(D2), .Q(Q2));  // open: Q_2
  level_trig_D_type_Flip_Flop level_trig_d_type_flip_flop_7 (.Hold_That_Bit(Clk), .Data(D1), .Q(Q1));  // open: Q_2
  level_trig_D_type_Flip_Flop level_trig_d_type_flip_flop_8 (.Hold_That_Bit(Clk), .Data(D0), .Q(Q0));  // open: Q_2
endmodule
