// Digital circuit Eight_Bit_Adder.dig as structural Verilog
module Eight_Bit_Adder (
  input  ci,
  input  a0,
  input  b0,
  input  a1,
  input  b1,
  input  a2,
  input  a3,
  input  a4,
  input  a5,
  input  a6,
  input  a7,
  input  b2,
  input  b3,
  input  b4,
  input  b5,
  input  b6,
  input  b7,
  output o0,
  output o1,
  output o2,
  output o3,
  output o4,
  output o5,
  output o6,
  output o7,
  output co
);

  wire full_adder__omo_1_co, full_adder__omo_2_co, full_adder__omo_3_co, full_adder__omo_4_co,
       full_adder__omo_5_co, full_adder__omo_6_co, full_adder__omo_7_co;

  Full_Adder__OMO full_adder__omo_1 (.Bin(b0), .Ain(a0), .Cin(ci), .So(o0), .Co(full_adder__omo_1_co));
  Full_Adder__OMO full_adder__omo_2 (
    .Bin(b1), .Ain(a1), .Cin(full_adder__omo_1_co), .So(o1), .Co(full_adder__omo_2_co));
  Full_Adder__OMO full_adder__omo_3 (
    .Bin(b2), .Ain(a2), .Cin(full_adder__omo_2_co), .So(o2), .Co(full_adder__omo_3_co));
  Full_Adder__OMO full_adder__omo_4 (
    .Bin(b3), .Ain(a3), .Cin(full_adder__omo_3_co), .So(o3), .Co(full_adder__omo_4_co));
  Full_Adder__OMO full_adder__omo_5 (
    .Bin(b4), .Ain(a4), .Cin(full_adder__omo_4_co), .So(o4), .Co(full_adder__omo_5_co));
  Full_Adder__OMO full_adder__omo_6 (
    .Bin(b5), .Ain(a5), .Cin(full_adder__omo_5_co), .So(o5), .Co(full_adder__omo_6_co));
  Full_Adder__OMO full_adder__omo_7 (
    .Bin(b6), .Ain(a6), .Cin(full_adder__omo_6_co), .So(o6), .Co(full_adder__omo_7_co));
  Full_Adder__OMO full_adder__omo_8 (.Bin(b7), .Ain(a7), .Cin(full_adder__omo_7_co), .So(o7), .Co(co));
endmodule
