// Digital circuit Full_Adder_ OMO.dig as structural Verilog
module Full_Adder__OMO (
  input  Bin,
  input  Ain,
  input  Cin,
  output So,
  output Co
);

  wire half_adder_omo_1_carry, half_adder_omo_1_sum, half_adder_omo_2_carry;

  Half_Adder_OMO half_adder_omo_1 (.Ain(Ain), .Bin(Bin), .Carry(half_adder_omo_1_carry), .Sum(half_adder_omo_1_sum));
  Half_Adder_OMO half_adder_omo_2 (.Ain(Cin), .Bin(half_adder_omo_1_sum), .Carry(half_adder_omo_2_carry), .Sum(So));
  or or_1 (Co, half_adder_omo_2_carry, half_adder_omo_1_carry);
endmodule
