// Digital circuit Half_Adder_OMO.dig as structural Verilog
module Half_Adder_OMO (
  input  Ain,
  input  Bin,
  output Carry,
  output Sum
);

  xorOnMyOwn xoronmyown_1 (.Ain(Ain), .Bin(Bin), .out(Sum));
  and and_1 (Carry, Ain, Bin);
endmodule
