// Digital circuit Ones_Comp.dig as structural Verilog
module Ones_Comp (
  input  Invert,
  input  i7,
  input  i6,
  input  i5,
  input  i4,
  input  i3,
  input  i2,
  input  i1,
  input  i0,
  output o7,
  output o6,
  output o5,
  output o4,
  output o3,
  output o2,
  output o1,
  output o0
);

  xor xor_1 (o7, i7, Invert);
  xor xor_2 (o6, i6, Invert);
  xor xor_3 (o5, i5, Invert);
  xor xor_4 (o4, i4, Invert);
  xor xor_5 (o3, i3, Invert);
  xor xor_6 (o2, i2, Invert);
  xor xor_7 (o1, i1, Invert);
  xor xor_8 (o0, i0, Invert);
endmodule
