// Digital circuit R-S-Flip-Flop-Box.dig as structural Verilog
module R_S_Flip_Flop_Box (
  input  in_1,
  input  in_2,
  output out_3,
  output out_4
);

  R_S_flip_flop r_s_flip_flop_1 (.R(in_1), .S(in_2), .Q(out_3), .Q_2(out_4));
endmodule
