// Digital circuit demux.dig as structural Verilog
module demux (
  input  In,
  input  Sel,
  output A,
  output B
);

  wire not_1_out;

  not not_1 (not_1_out, Sel);
  and and_1 (A, In, not_1_out);
  and and_2 (B, In, Sel);
endmodule
