// Digital circuit full_adder.dig as structural Verilog
module full_adder (
  input  Carryin,
  input  A_in,
  input  B_in,
  output Out_A,
  output Out_B
);

  wire half_adder_1_carry_out, half_adder_1_sum_out, half_adder_2_carry_out;

  half_adder half_adder_1 (.Ain(A_in), .Bin(B_in), .Sum_out(half_adder_1_sum_out), .Carry_out(half_adder_1_carry_out));
  half_adder half_adder_2 (
    .Ain(Carryin), .Bin(half_adder_1_sum_out), .Sum_out(Out_A), .Carry_out(half_adder_2_carry_out));
  or or_1 (Out_B, half_adder_2_carry_out, half_adder_1_carry_out);
endmodule
