// Digital circuit half_adder.dig as structural Verilog
module half_adder (
  input  Ain,
  input  Bin,
  output Sum_out,
  output Carry_out
);

  \xor  xor_1 (.InA(Ain), .InB(Bin), .Out(Sum_out));
  and and_1 (Carry_out, Ain, Bin);
endmodule
