// Digital circuit ripple-box.dig as structural Verilog
module ripple_box (
  input  Q0,
  input  Q1,
  input  Q2,
  input  Q3,
  input  Q4,
  input  Q5,
  input  Q6,
  input  Q7,
  input  in_10,
  output Clk
);

  wire edge_triggered_flip_flop_1_q_bar, edge_triggered_flip_flop_2_q_bar, edge_triggered_flip_flop_3_q_bar,
       edge_triggered_flip_flop_4_q_bar, edge_triggered_flip_flop_5_q_bar, edge_triggered_flip_flop_6_q_bar,
       edge_triggered_flip_flop_7_q_bar, edge_triggered_flip_flop_8_q_bar;

  not not_1 (in_10, Clk);
  Edge_Triggered_Flip_Flop edge_triggered_flip_flop_1 (
    .Data(edge_triggered_flip_flop_1_q_bar), .Clock(Clk), .Q(Q0), .Q_BAR(edge_triggered_flip_flop_1_q_bar));
  Edge_Triggered_Flip_Flop edge_triggered_flip_flop_2 (
    .Data(edge_triggered_flip_flop_2_q_bar), .Clock(edge_triggered_flip_flop_1_q_bar), .Q(Q1),
    .Q_BAR(edge_triggered_flip_flop_2_q_bar));
  Edge_Triggered_Flip_Flop edge_triggered_flip_flop_3 (
    .Data(edge_triggered_flip_flop_3_q_bar), .Clock(edge_triggered_flip_flop_2_q_bar), .Q(Q2),
    .Q_BAR(edge_triggered_flip_flop_3_q_bar));
  Edge_Triggered_Flip_Flop edge_triggered_flip_flop_4 (
    .Data(edge_triggered_flip_flop_4_q_bar), .Clock(edge_triggered_flip_flop_3_q_bar), .Q(Q3),
    .Q_BAR(edge_triggered_flip_flop_4_q_bar));
  Edge_Triggered_Flip_Flop edge_triggered_flip_flop_5 (
    .Data(edge_triggered_flip_flop_5_q_bar), .Clock(edge_triggered_flip_flop_4_q_bar), .Q(Q4),
    .Q_BAR(edge_triggered_flip_flop_5_q_bar));
  Edge_Triggered_Flip_Flop edge_triggered_flip_flop_6 (
    .Data(edge_triggered_flip_flop_6_q_bar), .Clock(edge_triggered_flip_flop_5_q_bar), .Q(Q5),
    .Q_BAR(edge_triggered_flip_flop_6_q_bar));
  Edge_Triggered_Flip_Flop edge_triggered_flip_flop_7 (
    .Data(edge_triggered_flip_flop_7_q_bar), .Clock(edge_triggered_flip_flop_6_q_bar), .Q(Q6),
    .Q_BAR(edge_triggered_flip_flop_7_q_bar));
  Edge_Triggered_Flip_Flop edge_triggered_flip_flop_8 (
    .Data(edge_triggered_flip_flop_8_q_bar), .Clock(edge_triggered_flip_flop_7_q_bar), .Q(Q7),
    .Q_BAR(edge_triggered_flip_flop_8_q_bar));
endmodule
