// Digital circuit twoNORtwoSWITCHFeedback.dig as structural Verilog
module twoNORtwoSWITCHFeedback (
  input  in_1,
  input  in_2,
  output out_3
);

  wire nor_1_out;

  nor nor_1 (nor_1_out, out_3, in_1);
  nor nor_2 (out_3, nor_1_out, in_2);
endmodule
